# Fritzing sketch sketch (saved by Fritzing 0.9.3b)
circuit board: 8.46667cm x 5.64444cm
breadboards: 1

parts:
  Part1 = Arduino Uno (Rev3)
  R1 = Resistor [tolerance=±5% resistance=330 package=THT]
  R2 = Resistor [tolerance=±5% resistance=330 package=THT]
  R3 = Resistor [tolerance=±5% resistance=330 package=THT]
  LED1 = LED - 5mm [color="Red (633nm)" package="5 mm [THT]"]
  LED2 = LED - 5mm [color="Red (633nm)" package="5 mm [THT]"]
  LED3 = LED - 5mm [color="Red (633nm)" package="5 mm [THT]"]
  Part2 = Breakout Board for Electret Microphone

nets:
  N1: Part1.A0, Part2.VCC
  GND: Part1.GND, R1.Pin_0, R2.Pin_0, R3.Pin_0, Part2.GND
  N2: Part1.D3_PWM, LED3.anode
  N3: Part1.D5_PWM, LED2.anode
  N4: Part1.D7, LED1.anode
  N5: Part1.5V, Part2.AUD
  N6: R1.Pin_1, LED3.cathode
  N7: R2.Pin_1, LED2.cathode
  N8: R3.Pin_1, LED1.cathode
